# Fritzing sketch schema (saved by Fritzing 0.9.4)

parts:
  M1 = DC Motor
  Mod1 = KY-022 Infrared Receiver Module [package="Breakout board"]
  Part2 = AF_mshield-v1.2_breadboard
  Part1 = Arduino Uno (Rev3)
  J1 = Basic Servo

nets:
  N1: M1.pin_1, Part2.3, Part2.P5
  N2: M1.pin_2, Part2.1, Part2.P4
  N3: Mod1.-, Part1.GND
  VIN: Mod1.Vin, Part1.5V
  N4: Mod1.S, Part1.D11_PWM/MOSI
  N5: Part2.PWM1B, J1.pulse
  VCC: Part2.VCC, J1.vcc
  GND: Part2.GND, J1.gnd

custom parts:
  KY-022 Infrared Receiver Module: KY-022 IR receiver module, reacts to 38kHz infrared light.
  : motor Shield v1 Adafruit Adafruit Motor/Stepper/Servo Shield for Arduino kit [v1.2] : ID 81 : $19.50 : Adafruit Industries, Unique & fun DIY electronics and kits
